// Logisim project cpu.circ as structural Verilog: 2 circuits, main circuit main
module main (
  input  [15:0] INSTRUCTION,
  input  CLOCK,
  output [15:0] FETCH_ADDRESS,
  output [15:0] L_s0_Value_7c9fba82,
  output [15:0] L_s1_Value_2cb75696,
  output [15:0] L_s2_Value_be7b1681,
  output [15:0] L_ra_Value_55886cf9,
  output [15:0] L_sp_Value_a0856b3d,
  output [15:0] L_HI_Value_3bde5b98,
  output [15:0] L_LO_Value_b62659ce
);

  wire EQUAL, MEM_p3, WRITE_EN_RAM, WRITE_EN_REG;
  wire [2:0] SWITCH;
  wire [15:0] control_unit_cpu_1_alu_x, control_unit_cpu_1_alu_y, HI, LO, PC;

  Register #(.width(16)) L_PC_bd1e00e6 (.Q(PC));  // open: D, en, clk, clr
  Register #(.width(16)) L_LO_ba622f5d (.Q(LO));  // open: D, en, clk, clr
  Register #(.width(16)) L_HI_1d3f3066 (.Q(HI));  // open: D, en, clk, clr
  regfile_main main_1 (
    .L_s0_Value_3e1de553(L_s0_Value_7c9fba82), .L_s1_Value_f16d02bf(L_s1_Value_2cb75696),
    .L_s2_Value_6a9ed51f(L_s2_Value_be7b1681), .L_ra_Value_b804995d(L_ra_Value_55886cf9),
    .L_sp_Value_269f0ffd(L_sp_Value_a0856b3d), .Write_Enable_5f560963(WRITE_EN_REG), .Clock(CLOCK));  // open: Read_Data_1_c47ea0d8, Read_Data_2_34b29906, Read_Register_1_eca808b4, Read_Register_2_4b336a3e, Write_Register_1c78e1ef, Write_Data_00073c80
  // mem_main MEM: pin names not known; wires that end beside it: WRITE_EN_RAM, CLOCK, MEM_p3
  CONTROL_UNIT_CPU control_unit_cpu_1 (
    .PC(PC), .EQUAL(EQUAL), .INSTR(INSTRUCTION), .WRITE_EN_RAM(WRITE_EN_RAM), .WRITE_EN_REG(WRITE_EN_REG),
    .ALU_SWITCH(SWITCH), .ALU_X(control_unit_cpu_1_alu_x), .ALU_Y(control_unit_cpu_1_alu_y),
    .FETCH_ADDR(FETCH_ADDRESS));  // open: RAM_ADDR_R, RAM_ADDR_WR, REG_ADDR_R1, REG_ADDR_R2, REG_ADDR_WR
  alu_main main_2 (
    .Equal(EQUAL), .X(control_unit_cpu_1_alu_x), .Y(control_unit_cpu_1_alu_y));  // open: Result, Result_2_a9898de3, Switch

  // Other names for the same wires on the sheet: clk = CLOCK; fetch_addr[15:0] = FETCH_ADDRESS

  // Notes on the sheet:
  //   Output
  //   These are outputs/inputs from run.circ
  //   Inputs
  //   These are DEBUG/TEST outputs from your circuit.
endmodule

// RD_AA
module CONTROL_UNIT_CPU (
  input  [15:0] PC,
  input  EQUAL,
  input  [15:0] INSTR,
  output WRITE_EN_RAM,
  output WRITE_EN_REG,
  output [2:0] ALU_SWITCH,
  output [15:0] ALU_X,
  output [15:0] ALU_Y,
  output [15:0] RAM_ADDR_R,
  output [15:0] RAM_ADDR_WR,
  output [2:0] REG_ADDR_R1,
  output [2:0] REG_ADDR_R2,
  output [2:0] REG_ADDR_WR,
  output [15:0] FETCH_ADDR
);

  wire demultiplexer_1_out0, demultiplexer_2_out0;
  wire [15:0] bit_extender_1_out, BRANCH_ADDR, multiplexer_1_out, multiplexer_2_out, PCPLUS2;

  assign bit_extender_1_out = {{10{INSTR[5]}}, INSTR[5:0]};  // Bit_Extender bit_extender_1
  Multiplexer #(.width(16), .enable("false")) multiplexer_1 (
    .in0(BRANCH_ADDR), .in1(PCPLUS2), .out(multiplexer_1_out), .sel(EQUAL));
  Adder #(.width(16)) adder_1 (.a(PC), .b(bit_extender_1_out), .out(BRANCH_ADDR));  // open: cin, cout
  Multiplexer #(.width(16), .enable("false")) multiplexer_2 (
    .in0(PCPLUS2), .in1(BRANCH_ADDR), .out(multiplexer_2_out), .sel(EQUAL));
  Adder #(.width(16)) adder_2 (.a(PC), .b(16'h2), .out(PCPLUS2));  // open: cin, cout
  Multiplexer #(.select(4), .width(16), .enable("false")) multiplexer_3 (
    .in0(PCPLUS2), .in1(PCPLUS2), .in2({PC[15:10], INSTR[9:0]}), .in4(multiplexer_2_out),
    .in5(multiplexer_1_out), .in6(PCPLUS2), .in7(PCPLUS2), .in8(PCPLUS2), .in9(PCPLUS2), .in10(PCPLUS2),
    .in11(PCPLUS2), .in12(PCPLUS2), .in13(PCPLUS2), .in14(PCPLUS2), .in15(PCPLUS2), .out(FETCH_ADDR),
    .sel(INSTR[15:12]));  // open: in3
  Demultiplexer #(.select(4), .enable("false")) demultiplexer_1 (
    .out0(demultiplexer_1_out0), .in(1'b1), .sel(INSTR[15:12]));  // open: out1, out2, out3, out4, out5, out6, out7, out8, out9, out10, out11, out12, out13, out14, out15
  Demultiplexer #(.select(3), .enable("false")) demultiplexer_2 (
    .out0(demultiplexer_2_out0), .in(demultiplexer_1_out0), .sel(INSTR[2:0]));  // open: out1, out2, out3, out4, out5, out6, out7
  Multiplexer #(.width(16), .enable("false")) multiplexer_4 (
    .in0({{10{1'b0}}, INSTR[5:0]}), .out(ALU_Y), .sel(demultiplexer_1_out0));  // open: in1
  Multiplexer #(.width(3), .enable("false")) multiplexer_5 (
    .in1(INSTR[2:0]), .out(ALU_SWITCH), .sel(demultiplexer_1_out0));  // open: in0

  // Other names for the same wires on the sheet: FUNCT[2:0] = INSTR[2:0]; IMME_I[5:0] = INSTR[5:0];
  //   IMME_U[9:0] = INSTR[9:0]; JUMP[15:0] = {PC[15:10], INSTR[9:0]}; RT_ADDR[2:0] = INSTR[5:3];
  //   RS_ADDR[2:0] = INSTR[8:6]; RD_ADDR[2:0] = INSTR[11:9]; RDU_ADDR[1:0] = INSTR[11:10]; OPCODE[3:0] = INSTR[15:12]

  // Notes on the sheet:
  //   SELECT OPCODE
  //   0 = type R
  //   SELECT FUNCT
  //   SLL
  //   On r-type,  X is rs and Y is rt
endmodule
