// Logisim project regfile.circ as structural Verilog
module main (
  input  [2:0] Read_Register_1_eca808b4,
  input  [2:0] Read_Register_2_4b336a3e,
  input  [2:0] Write_Register_1c78e1ef,
  input  [15:0] Write_Data_00073c80,
  input  Write_Enable_5f560963,
  input  Clock,
  output [15:0] L_s0_Value_3e1de553,
  output [15:0] L_s1_Value_f16d02bf,
  output [15:0] L_s2_Value_6a9ed51f,
  output [15:0] L_ra_Value_b804995d,
  output [15:0] L_sp_Value_269f0ffd,
  output [15:0] Read_Data_1_c47ea0d8,
  output [15:0] Read_Data_2_34b29906
);

  Register #(.width(32)) register_1 (.clk(Clock));  // open: D, en, Q, clr
  Register #(.width(32)) register_2 (.clk(Clock));  // open: D, en, Q, clr
  Register #(.width(32)) register_3 (.clk(Clock));  // open: D, en, Q, clr
  Register #(.width(32)) register_4 (.clk(Clock));  // open: D, en, Q, clr
  Register #(.width(32)) register_5 (.clk(Clock));  // open: D, en, Q, clr
  Register #(.width(32)) register_6 (.clk(Clock));  // open: D, en, Q, clr
  Register #(.width(32)) register_7 (.clk(Clock));  // open: D, en, Q, clr
  Register #(.width(32)) register_8 (.clk(Clock));  // open: D, en, Q, clr

  // Other names for the same wires on the sheet: clk = Clock; read_data1[15:0] = Read_Data_1_c47ea0d8;
  //   read_data2[15:0] = Read_Data_2_34b29906; read_reg1[2:0] = Read_Register_1_eca808b4;
  //   read_reg2[2:0] = Read_Register_2_4b336a3e; write_data[15:0] = Write_Data_00073c80;
  //   write_en = Write_Enable_5f560963; write_reg[2:0] = Write_Register_1c78e1ef

  // Notes on the sheet:
  //   INPUTS to your circuit
  //   DON'T CHANGE THE LOCATIONS OF THE INPUTS AND OUTPUTS!
  //   These are DEBUG/TEST outputs from your circuit.
  //   OUTPUTS from your circuit
endmodule
